# Fritzing sketch GestureControlled (saved by Fritzing 0.8.7b)
breadboards: 2

parts:
  U1 = NodeMCU V3.0
  LED1 = RGB LED (com. anode, rbg) [package="5 mm [THT]"]
  GY1 = MPU-6050 Board GY-521 [form="♀ (female)" package=THT]
  U2 = LIPO-1000mAh [package=lipo-1000]

nets:
  N1: U1.D0, LED1.red_cathode
  N2: U1.D1, LED1.common_anode
  N3: U1.D2, LED1.green_cathode
  N4: U1.3V3, LED1.blue_cathode, GY1.pin1
  N5: U1.GND#6, U1.GND#13, U1.GND#16, U1.GND#33, GY1.pin2, U2.-
  N6: U1.D5, GY1.pin3
  N7: U1.D6, GY1.pin4
  N8: U1.Vin, U2.+

custom parts:
  NodeMCU V3.0: ESP8266 based NodeMCU
  MPU-6050 Board GY-521: Acelerometro y Giroscopio MPU-6050 Board GY-521
